// Logisim project 8 bit Microprocessor Abdul Raffay Final Project.circ as structural Verilog: 10 circuits, main circuit main
module main (
  input  [7:0] Testing_Data,
  input  OE,
  input  OE_Testing_Data,
  input  [3:0] OE_Testing_Data_2,
  input  [2:0] ALU_Function_Selector,
  output [3:0] MAR_Content,
  output [3:0] Content_of_Counter,
  output [7:0] IR_Content,
  output [7:0] MBR_Content,
  output [7:0] Reg_A_Content,
  output [7:0] ALU_Result,
  output [7:0] out_12,
  output [3:0] out_13,
  output [7:0] Reg_B_Content,
  output [2:0] Content_of_Counter_2
);

  wire c0, c1, c2, c3, c4, c5, c6, c7, c8, c9, c10, c11, c12, c13, c14, c15, clock;
  wire [3:0] controlled_buffer_1_out, Decimal_Decoder_4_data_output, Decimal_Decoder_4_data_output_2,
       Decimal_Decoder_4_data_output_3, Decimal_Decoder_4_data_output_4, Decimal_Decoder_4_data_output_5,
       Decimal_Decoder_4_data_output_6, Decimal_Decoder_4_data_output_7, Decimal_Decoder_4_data_output_8,
       MAR_data_output;
  wire [7:0] alu_1_data_output, bit_extender_1_out, bit_extender_2_out, Instruction_Register_data_output;
  wire [31:0] Decimal_Decoder_2_data_output, Decimal_Decoder_3_data_output, Decimal_Decoder_5_data_output,
       Decimal_Decoder_data_output;

  Clock clock_1 (.out(clock));
  Counter #(.width(4), .max('hf)) Program_Counter (
    .D(controlled_buffer_1_out), .count(c1), .Q(Content_of_Counter), .clk(clock));  // open: load, carry, clr
  Register Instruction_Register (
    .Clock(clock), .Write_Enable(c7), .Data_Input(alu_1_data_output), .Output_Enable(c8),
    .Data_Output(Instruction_Register_data_output), .Stored_Data(IR_Content));
  Register Register_A (
    .Clock(clock), .Write_Enable(c12), .Data_Input(alu_1_data_output), .Stored_Data(Reg_A_Content));  // open: Output_Enable, Data_Output
  Decimal_Decoder Decimal_Decoder (.Data_input(Reg_A_Content), .Data_Output(Decimal_Decoder_data_output));
  ALU alu_1 (
    .Data_Output(alu_1_data_output), .Function_Selector(ALU_Function_Selector), .Reg_A(Reg_A_Content),
    .Reg_B(Reg_B_Content), .Output_Enable(c11), .ALU_Result(ALU_Result));  // open: Carry_out_plus, Carry_out_minus, Carry_out_x, Carry_out
  Register Register_B (
    .Clock(clock), .Write_Enable(c13), .Data_Input(alu_1_data_output), .Stored_Data(Reg_B_Content));  // open: Output_Enable, Data_Output
  assign controlled_buffer_1_out = c0 ? Content_of_Counter : 4'bz;  // Controlled_Buffer controlled_buffer_1
  assign bit_extender_1_out = {{4{1'b0}}, Content_of_Counter};  // Bit_Extender bit_extender_1
  Decimal_Decoder Decimal_Decoder_2 (.Data_input(bit_extender_1_out), .Data_Output(Decimal_Decoder_2_data_output));
  _7_Segment_Display u_7_segment_display_1 (
    .g(Decimal_Decoder_data_output[15]), .f(Decimal_Decoder_data_output[14]),
    .a(Decimal_Decoder_data_output[13]), .b(Decimal_Decoder_data_output[12]),
    .e(Decimal_Decoder_data_output[31]), .d(Decimal_Decoder_data_output[30]),
    .c(Decimal_Decoder_data_output[29]), .dp(Decimal_Decoder_data_output[28]));
  Decimal_Decoder Decimal_Decoder_3 (.Data_input(Reg_B_Content), .Data_Output(Decimal_Decoder_3_data_output));
  _7_Segment_Display u_7_segment_display_2 (
    .g(Decimal_Decoder_2_data_output[3]), .f(Decimal_Decoder_2_data_output[2]),
    .a(Decimal_Decoder_2_data_output[1]), .b(Decimal_Decoder_2_data_output[0]),
    .e(Decimal_Decoder_2_data_output[19]), .d(Decimal_Decoder_2_data_output[18]),
    .c(Decimal_Decoder_2_data_output[17]), .dp(Decimal_Decoder_2_data_output[16]));
  _7_Segment_Display u_7_segment_display_3 (
    .g(Decimal_Decoder_data_output[7]), .f(Decimal_Decoder_data_output[6]),
    .a(Decimal_Decoder_data_output[5]), .b(Decimal_Decoder_data_output[4]),
    .e(Decimal_Decoder_data_output[23]), .d(Decimal_Decoder_data_output[22]),
    .c(Decimal_Decoder_data_output[21]), .dp(Decimal_Decoder_data_output[20]));
  _7_Segment_Display u_7_segment_display_4 (
    .g(Decimal_Decoder_data_output[11]), .f(Decimal_Decoder_data_output[10]),
    .a(Decimal_Decoder_data_output[9]), .b(Decimal_Decoder_data_output[8]),
    .e(Decimal_Decoder_data_output[27]), .d(Decimal_Decoder_data_output[26]),
    .c(Decimal_Decoder_data_output[25]), .dp(Decimal_Decoder_data_output[24]));
  _7_Segment_Display u_7_segment_display_5 (
    .g(Decimal_Decoder_3_data_output[15]), .f(Decimal_Decoder_3_data_output[14]),
    .a(Decimal_Decoder_3_data_output[13]), .b(Decimal_Decoder_3_data_output[12]),
    .e(Decimal_Decoder_3_data_output[31]), .d(Decimal_Decoder_3_data_output[30]),
    .c(Decimal_Decoder_3_data_output[29]), .dp(Decimal_Decoder_3_data_output[28]));
  _7_Segment_Display u_7_segment_display_6 (
    .g(Decimal_Decoder_3_data_output[11]), .f(Decimal_Decoder_3_data_output[10]),
    .a(Decimal_Decoder_3_data_output[9]), .b(Decimal_Decoder_3_data_output[8]),
    .e(Decimal_Decoder_3_data_output[27]), .d(Decimal_Decoder_3_data_output[26]),
    .c(Decimal_Decoder_3_data_output[25]), .dp(Decimal_Decoder_3_data_output[24]));
  BitSelector #(.group(4)) bitselector_1 (
    .in(Instruction_Register_data_output), .out(controlled_buffer_1_out), .sel(1'b0));
  _7_Segment_Display u_7_segment_display_7 (
    .g(Decimal_Decoder_data_output[3]), .f(Decimal_Decoder_data_output[2]),
    .a(Decimal_Decoder_data_output[1]), .b(Decimal_Decoder_data_output[0]),
    .e(Decimal_Decoder_data_output[19]), .d(Decimal_Decoder_data_output[18]),
    .c(Decimal_Decoder_data_output[17]), .dp(Decimal_Decoder_data_output[16]));
  _7_Segment_Display u_7_segment_display_8 (
    .g(Decimal_Decoder_3_data_output[7]), .f(Decimal_Decoder_3_data_output[6]),
    .a(Decimal_Decoder_3_data_output[5]), .b(Decimal_Decoder_3_data_output[4]),
    .e(Decimal_Decoder_3_data_output[23]), .d(Decimal_Decoder_3_data_output[22]),
    .c(Decimal_Decoder_3_data_output[21]), .dp(Decimal_Decoder_3_data_output[20]));
  _7_Segment_Display u_7_segment_display_9 (
    .g(Decimal_Decoder_3_data_output[3]), .f(Decimal_Decoder_3_data_output[2]),
    .a(Decimal_Decoder_3_data_output[1]), .b(Decimal_Decoder_3_data_output[0]),
    .e(Decimal_Decoder_3_data_output[19]), .d(Decimal_Decoder_3_data_output[18]),
    .c(Decimal_Decoder_3_data_output[17]), .dp(Decimal_Decoder_3_data_output[16]));
  LED D7 (.in(alu_1_data_output[7]));
  LED D6 (.in(alu_1_data_output[6]));
  assign alu_1_data_output = OE_Testing_Data ? Testing_Data : 8'bz;  // Controlled_Buffer controlled_buffer_2
  LED D3 (.in(alu_1_data_output[3]));
  LED D4 (.in(alu_1_data_output[4]));
  LED D5 (.in(alu_1_data_output[5]));
  LED D2 (.in(alu_1_data_output[2]));
  LED D1 (.in(alu_1_data_output[1]));
  LED D0 (.in(alu_1_data_output[0]));
  MAR MAR (
    .Clock(clock), .Write_Enable(c9), .Data_Input(controlled_buffer_1_out), .Output_Enable(c10),
    .Data_Output(MAR_data_output), .Stored_Data(MAR_Content));
  assign alu_1_data_output = c5 ? MBR_Content : 8'bz;  // Controlled_Buffer controlled_buffer_3
  Register MDR_MBR (
    .Clock(clock), .Write_Enable(c4), .Data_Input(alu_1_data_output), .Output_Enable(c6),
    .Data_Output(alu_1_data_output), .Stored_Data(MBR_Content));
  Register Output_Register (
    .Clock(clock), .Write_Enable(c15), .Data_Input(alu_1_data_output), .Output_Enable(c14),
    .Data_Output(alu_1_data_output), .Stored_Data(out_12));
  Decimal_Decoder Decimal_Decoder_4 (
    .Data_input(out_12),
    .Data_Output({Decimal_Decoder_4_data_output_8, Decimal_Decoder_4_data_output_7, Decimal_Decoder_4_data_output_6, Decimal_Decoder_4_data_output_5, Decimal_Decoder_4_data_output_4, Decimal_Decoder_4_data_output_3, Decimal_Decoder_4_data_output_2, Decimal_Decoder_4_data_output}));
  _7_Segment_Display u_7_segment_display_10 (
    .g(Decimal_Decoder_4_data_output_4[3]), .f(Decimal_Decoder_4_data_output_4[2]),
    .a(Decimal_Decoder_4_data_output_4[1]), .b(Decimal_Decoder_4_data_output_4[0]),
    .e(Decimal_Decoder_4_data_output_8[3]), .d(Decimal_Decoder_4_data_output_8[2]),
    .c(Decimal_Decoder_4_data_output_8[1]), .dp(Decimal_Decoder_4_data_output_8[0]));
  assign MAR_data_output = OE ? OE_Testing_Data_2 : 4'bz;  // Controlled_Buffer controlled_buffer_4
  _7_Segment_Display u_7_segment_display_11 (
    .g(Decimal_Decoder_4_data_output_2[3]), .f(Decimal_Decoder_4_data_output_2[2]),
    .a(Decimal_Decoder_4_data_output_2[1]), .b(Decimal_Decoder_4_data_output_2[0]),
    .e(Decimal_Decoder_4_data_output_6[3]), .d(Decimal_Decoder_4_data_output_6[2]),
    .c(Decimal_Decoder_4_data_output_6[1]), .dp(Decimal_Decoder_4_data_output_6[0]));
  _7_Segment_Display u_7_segment_display_12 (
    .g(Decimal_Decoder_4_data_output_3[3]), .f(Decimal_Decoder_4_data_output_3[2]),
    .a(Decimal_Decoder_4_data_output_3[1]), .b(Decimal_Decoder_4_data_output_3[0]),
    .e(Decimal_Decoder_4_data_output_7[3]), .d(Decimal_Decoder_4_data_output_7[2]),
    .c(Decimal_Decoder_4_data_output_7[1]), .dp(Decimal_Decoder_4_data_output_7[0]));
  _7_Segment_Display u_7_segment_display_13 (
    .g(Decimal_Decoder_4_data_output[3]), .f(Decimal_Decoder_4_data_output[2]),
    .a(Decimal_Decoder_4_data_output[1]), .b(Decimal_Decoder_4_data_output[0]),
    .e(Decimal_Decoder_4_data_output_5[3]), .d(Decimal_Decoder_4_data_output_5[2]),
    .c(Decimal_Decoder_4_data_output_5[1]), .dp(Decimal_Decoder_4_data_output_5[0]));
  LED D5_2 (.in(alu_1_data_output[5]));
  LED D6_2 (.in(alu_1_data_output[6]));
  LED D7_2 (.in(alu_1_data_output[7]));
  LED D1_2 (.in(alu_1_data_output[1]));
  LED D4_2 (.in(alu_1_data_output[4]));
  LED D2_2 (.in(alu_1_data_output[2]));
  LED D3_2 (.in(alu_1_data_output[3]));
  LED D0_2 (.in(alu_1_data_output[0]));
  BitSelector #(.group(4)) bitselector_2 (.in(IR_Content), .out(out_13), .sel(1'b1));
  Counter #(.width(3), .max('h5)) Step_Counter (
    .Q(Content_of_Counter_2), .clk(clock));  // open: load, D, count, carry, clr
  RAM #(.addrWidth(4), .bus("separate")) ram_1 (
    .addr(MAR_data_output), .din(alu_1_data_output), .data(alu_1_data_output), .str(c2), .clk(clock), .ld(c3));  // open: sel, clr
  assign bit_extender_2_out = {{5{1'b0}}, Content_of_Counter_2};  // Bit_Extender bit_extender_2
  Decimal_Decoder Decimal_Decoder_5 (.Data_input(bit_extender_2_out), .Data_Output(Decimal_Decoder_5_data_output));
  CU_1 cu_1_1 (
    .OPC3(out_13[3]), .OPC2(out_13[2]), .OPC1(out_13[1]), .OPC0(out_13[0]), .SC2(Content_of_Counter_2[2]),
    .SC1(Content_of_Counter_2[1]), .SC0(Content_of_Counter_2[0]), .C0(c0), .C1(c1), .C2(c2), .C3(c3),
    .C4(c4), .C5(c5), .C6(c6), .C7(c7), .C8(c8), .C9(c9), .C10(c10), .C11(c11));
  CU_II CU_II (
    .OPC3(out_13[3]), .OPC2(out_13[2]), .OPC1(out_13[1]), .OPC0(out_13[0]), .SC2(Content_of_Counter_2[2]),
    .SC1(Content_of_Counter_2[1]), .SC0(Content_of_Counter_2[0]), .C12(c12), .C13(c13), .C14(c14), .C15(c15));
  _7_Segment_Display u_7_segment_display_14 (
    .g(Decimal_Decoder_5_data_output[3]), .f(Decimal_Decoder_5_data_output[2]),
    .a(Decimal_Decoder_5_data_output[1]), .b(Decimal_Decoder_5_data_output[0]),
    .e(Decimal_Decoder_5_data_output[19]), .d(Decimal_Decoder_5_data_output[18]),
    .c(Decimal_Decoder_5_data_output[17]), .dp(Decimal_Decoder_5_data_output[16]));

  // Other names for the same wires on the sheet: IR[7:0] = IR_Content

  // Notes on the sheet:
  //   Program Counter
  //   Internal Address Bus (4 bits)
  //   Internal Data Bus
  //   8- BIT COMPUTER 
  //   External Address Bus
  //   Internal Data Bus
  //   RAM
endmodule

module Memory_Cell (
  input  Clock,
  input  Write_Enable,
  input  Data_Input,
  input  Output_Enable,
  input  Reset,
  output Data_Output,
  output Stored_Data
);

  wire AND_2_out, AND_out, not_1_out, OR_out;

  not not_1 (not_1_out, Write_Enable);
  and AND (AND_out, Stored_Data, not_1_out);
  and AND_2 (AND_2_out, Write_Enable, Data_Input);
  or OR (OR_out, AND_out, AND_2_out);
  D_Flip_Flop D_Flip_flop (.clk(Clock), .D(OR_out), .Q(Stored_Data), .reset(Reset));  // open: Qn, preset, en
  assign Data_Output = Output_Enable ? Stored_Data : 1'bz;  // Controlled_Buffer controlled_buffer_1

  // Notes on the sheet:
  //   Memory Cell
endmodule

module Register (
  input  Clock,
  input  Write_Enable,
  input  [7:0] Data_Input,
  input  Output_Enable,
  output [7:0] Data_Output,
  output [7:0] Stored_Data
);

  Memory_Cell _0 (
    .Clock(Clock), .Write_Enable(Write_Enable), .Data_Input(Data_Input[0]), .Output_Enable(Output_Enable),
    .Data_Output(Data_Output[0]), .Stored_Data(Stored_Data[0]));  // open: Reset
  Memory_Cell _1 (
    .Clock(Clock), .Write_Enable(Write_Enable), .Data_Input(Data_Input[1]), .Output_Enable(Output_Enable),
    .Data_Output(Data_Output[1]), .Stored_Data(Stored_Data[1]));  // open: Reset
  Memory_Cell _2 (
    .Clock(Clock), .Write_Enable(Write_Enable), .Data_Input(Data_Input[2]), .Output_Enable(Output_Enable),
    .Data_Output(Data_Output[2]), .Stored_Data(Stored_Data[2]));  // open: Reset
  Memory_Cell _3 (
    .Clock(Clock), .Write_Enable(Write_Enable), .Data_Input(Data_Input[3]), .Output_Enable(Output_Enable),
    .Data_Output(Data_Output[3]), .Stored_Data(Stored_Data[3]));  // open: Reset
  Memory_Cell _4 (
    .Clock(Clock), .Write_Enable(Write_Enable), .Data_Input(Data_Input[4]), .Output_Enable(Output_Enable),
    .Data_Output(Data_Output[4]), .Stored_Data(Stored_Data[4]));  // open: Reset
  Memory_Cell _5 (
    .Clock(Clock), .Write_Enable(Write_Enable), .Data_Input(Data_Input[5]), .Output_Enable(Output_Enable),
    .Data_Output(Data_Output[5]), .Stored_Data(Stored_Data[5]));  // open: Reset
  Memory_Cell _6 (
    .Clock(Clock), .Write_Enable(Write_Enable), .Data_Input(Data_Input[6]), .Output_Enable(Output_Enable),
    .Data_Output(Data_Output[6]), .Stored_Data(Stored_Data[6]));  // open: Reset
  Memory_Cell _7 (
    .Clock(Clock), .Write_Enable(Write_Enable), .Data_Input(Data_Input[7]), .Output_Enable(Output_Enable),
    .Data_Output(Data_Output[7]), .Stored_Data(Stored_Data[7]));  // open: Reset

  // Other names for the same wires on the sheet: c = Clock; d0 = Data_Input[0]; d1 = Data_Input[1];
  //   d2 = Data_Input[2]; d3 = Data_Input[3]; d4 = Data_Input[4]; d5 = Data_Input[5]; d6 = Data_Input[6];
  //   d7 = Data_Input[7]; o0 = Data_Output[0]; o1 = Data_Output[1]; o2 = Data_Output[2]; o3 = Data_Output[3];
  //   o4 = Data_Output[4]; o5 = Data_Output[5]; o6 = Data_Output[6]; o7 = Data_Output[7]; oe = Output_Enable;
  //   s0 = Stored_Data[0]; s1 = Stored_Data[1]; s2 = Stored_Data[2]; s3 = Stored_Data[3]; s4 = Stored_Data[4];
  //   s5 = Stored_Data[5]; s6 = Stored_Data[6]; s7 = Stored_Data[7]; w = Write_Enable

  // Notes on the sheet:
  //   Registers
endmodule

module MAR (
  input  Clock,
  input  Write_Enable,
  input  [3:0] Data_Input,
  input  Output_Enable,
  output [3:0] Data_Output,
  output [3:0] Stored_Data
);

  Memory_Cell _0 (
    .Clock(Clock), .Write_Enable(Write_Enable), .Data_Input(Data_Input[0]), .Output_Enable(Output_Enable),
    .Data_Output(Data_Output[0]), .Stored_Data(Stored_Data[0]));  // open: Reset
  Memory_Cell _1 (
    .Clock(Clock), .Write_Enable(Write_Enable), .Data_Input(Data_Input[1]), .Output_Enable(Output_Enable),
    .Data_Output(Data_Output[1]), .Stored_Data(Stored_Data[1]));  // open: Reset
  Memory_Cell _2 (
    .Clock(Clock), .Write_Enable(Write_Enable), .Data_Input(Data_Input[2]), .Output_Enable(Output_Enable),
    .Data_Output(Data_Output[2]), .Stored_Data(Stored_Data[2]));  // open: Reset
  Memory_Cell _3 (
    .Clock(Clock), .Write_Enable(Write_Enable), .Data_Input(Data_Input[3]), .Output_Enable(Output_Enable),
    .Data_Output(Data_Output[3]), .Stored_Data(Stored_Data[3]));  // open: Reset

  // Other names for the same wires on the sheet: c = Clock; d0 = Data_Input[0]; d1 = Data_Input[1];
  //   d2 = Data_Input[2]; d3 = Data_Input[3]; o0 = Data_Output[0]; o1 = Data_Output[1]; o2 = Data_Output[2];
  //   o3 = Data_Output[3]; oe = Output_Enable; s0 = Stored_Data[0]; s1 = Stored_Data[1]; s2 = Stored_Data[2];
  //   s3 = Stored_Data[3]; w = Write_Enable

  // Notes on the sheet:
  //   MAR
endmodule

module ALU (
  input  [7:0] Reg_A,
  input  [7:0] Reg_B,
  input  [2:0] Function_Selector,
  input  Output_Enable,
  output Carry_out_plus,
  output Carry_out_minus,
  output [7:0] Carry_out_x,
  output [7:0] Data_Output,
  output [7:0] Carry_out,
  output [7:0] ALU_Result
);

  wire [7:0] adder_1_out, AND_out, divider_1_out, multiplier_1_out, OR_out, subtractor_1_out, XOR_out;

  Adder adder_1 (.a(Reg_A), .b(Reg_B), .out(adder_1_out), .cout(Carry_out_plus));  // open: cin
  Subtractor subtractor_1 (.a(Reg_A), .b(Reg_B), .out(subtractor_1_out), .bout(Carry_out_minus));  // open: bin
  Multiplier multiplier_1 (.a(Reg_A), .b(Reg_B), .out(multiplier_1_out), .cout(Carry_out_x));  // open: cin
  Divider divider_1 (.a(Reg_A), .b(Reg_B), .out(divider_1_out), .rem(Carry_out));  // open: upper
  assign AND_out = Reg_A & Reg_B;  // AND_Gate AND, 8 bits wide
  assign OR_out = Reg_A | Reg_B;  // OR_Gate OR, 8 bits wide
  assign XOR_out = Reg_A ^ Reg_B;  // XOR_Gate XOR, 8 bits wide
  Multiplexer #(.select(3), .width(8)) multiplexer_1 (
    .in0(adder_1_out), .in1(subtractor_1_out), .in2(multiplier_1_out), .in3(divider_1_out), .in4(AND_out),
    .in5(OR_out), .in6(XOR_out), .out(ALU_Result), .sel(Function_Selector));  // open: in7, en
  assign Data_Output = Output_Enable ? ALU_Result : 8'bz;  // Controlled_Buffer controlled_buffer_1

  // Notes on the sheet:
  //   8-Bit ALU  
endmodule

module Decimal_Decoder (
  input  [7:0] Data_input,
  output [31:0] Data_Output
);

  ROM #(.dataWidth(32)) rom_1 (
    .addr(Data_input),
    .data({Data_Output[31:28], Data_Output[15:12], Data_Output[27:24], Data_Output[11:8], Data_Output[23:20], Data_Output[7:4], Data_Output[19:16], Data_Output[3:0]}));  // open: sel

  // Notes on the sheet:
  //   ROM
  //   Decimal Decoder
  //   contents of rom_1 (hex, n*v repeats v):
  //   e7 21 cb 6b 2d 6e ee 23 ef 2f 21e7 2121 21cb 216b 212d 216e 21ee 2123 21ef 212f cbe7 cb21 cbcb cb6b
  //   cb2d cb6e cbee cb23 cbef cb2f 6be7 6b21 6bcb 6b6b 6b2d 6b6e 6bee 6b23 6bef 6b2f 2de7 2d21 2dcb 2d6b
  //   2d2d 2d6e 2dee 2d23 2def 2d2f 6ee7 6e21 6ecb 6e6b 6e2d 6e6e 6eee 6e23 6eef 6e2f eee7 ee21 eecb ee6b
  //   ee2d ee6e eeee ee23 eeef ee2f 23e7 2321 23cb 236b 232d 236e 23ee 2323 23ef 232f efe7 ef21 efcb ef6b
  //   ef2d ef6e efee ef23 efef ef2f 2fe7 2f21 2fcb 2f6b 2f2d 2f6e 2fee 2f23 2fef 2f2f 21e7e7 21e721 21e7cb
  //   21e76b 21e72d 21e76e 21e7ee 21e723 21e7ef 21e72f 2121e7 212121 2121cb 21216b 21212d 21216e 2121ee
  //   212123 2121ef 21212f 21cbe7 21cb21 21cbcb 21cb6b 21cb2d 21cb6e 21cbee 21cb23 21cbef 21cb2f 216be7
  //   216b21 216bcb 216b6b 216b2d 216b6e 216bee 216b23 216bef 216b2f 212de7 212d21 212dcb 212d6b 212d2d
  //   212d6e 212dee 212d23 212def 212d2f 216ee7 216e21 216ecb 216e6b 216e2d 216e6e 216eee 216e23 216eef
  //   216e2f 21eee7 21ee21 21eecb 21ee6b 21ee2d 21ee6e 21eeee 21ee23 21eeef 21ee2f 2123e7 212321 2123cb
  //   21236b 21232d 21236e 2123ee 212323 2123ef 21232f 21efe7 21ef21 21efcb 21ef6b 21ef2d 21ef6e 21efee
  //   21ef23 21efef 21ef2f 212fe7 212f21 212fcb 212f6b 212f2d 212f6e 212fee 212f23 212fef 212f2f cbe7e7
  //   cbe721 cbe7cb cbe76b cbe72d cbe76e cbe7ee cbe723 cbe7ef cbe72f cb21e7 cb2121 cb21cb cb216b cb212d
  //   cb216e cb21ee cb2123 cb21ef cb212f cbcbe7 cbcb21 cbcbcb cbcb6b cbcb2d cbcb6e cbcbee cbcb23 cbcbef
  //   cbcb2f cb6be7 cb6b21 cb6bcb cb6b6b cb6b2d cb6b6e cb6bee cb6b23 cb6bef cb6b2f cb2de7 cb2d21 cb2dcb
  //   cb2d6b cb2d2d cb2d6e cb2dee cb2d23 cb2def cb2d2f cb6ee7 cb6e21 cb6ecb cb6e6b cb6e2d cb6e6e
endmodule

module CU_1 (
  input  OPC3,
  input  OPC2,
  input  OPC1,
  input  OPC0,
  input  SC2,
  input  SC1,
  input  SC0,
  output C0,
  output C1,
  output C2,
  output C3,
  output C4,
  output C5,
  output C6,
  output C7,
  output C8,
  output C9,
  output C10,
  output C11
);

  wire and_2_out, and_3_out, and_4_out, and_6_out, and_7_out, and_8_out, and_9_out, and_10_out, and_11_out,
       and_12_out, and_15_out, and_16_out, and_17_out, and_18_out, and_19_out, and_20_out, and_21_out,
       and_22_out, not_1_out, not_2_out, not_3_out, not_4_out, not_5_out, not_6_out, not_7_out, not_8_out,
       not_9_out, not_10_out, not_11_out, not_12_out, not_13_out, not_14_out, not_15_out, not_16_out,
       not_17_out, not_18_out, not_19_out, not_20_out, not_21_out, not_22_out, not_23_out, not_24_out,
       not_25_out, not_26_out, not_27_out, not_28_out, not_29_out, not_30_out, not_31_out, not_32_out,
       not_33_out, not_34_out, not_35_out, not_36_out, not_37_out, not_38_out, not_39_out, not_40_out,
       not_41_out, not_42_out, not_43_out, not_44_out, not_45_out, not_46_out, not_47_out, not_48_out;

  not not_1 (not_1_out, SC2);
  not not_2 (not_2_out, SC1);
  not not_3 (not_3_out, SC0);
  not not_4 (not_4_out, SC2);
  not not_5 (not_5_out, SC1);
  not not_6 (not_6_out, SC2);
  not not_7 (not_7_out, SC1);
  not not_8 (not_8_out, SC2);
  not not_9 (not_9_out, SC1);
  not not_10 (not_10_out, SC1);
  not not_11 (not_11_out, SC0);
  not not_12 (not_12_out, SC2);
  not not_13 (not_13_out, SC1);
  not not_14 (not_14_out, OPC1);
  not not_15 (not_15_out, SC1);
  not not_16 (not_16_out, SC0);
  not not_17 (not_17_out, SC2);
  not not_18 (not_18_out, SC1);
  not not_19 (not_19_out, OPC1);
  not not_20 (not_20_out, SC1);
  not not_21 (not_21_out, SC0);
  not not_22 (not_22_out, SC2);
  not not_23 (not_23_out, SC2);
  not not_24 (not_24_out, SC0);
  not not_25 (not_25_out, OPC1);
  not not_26 (not_26_out, SC1);
  not not_27 (not_27_out, SC1);
  not not_28 (not_28_out, SC0);
  not not_29 (not_29_out, SC2);
  not not_30 (not_30_out, SC0);
  not not_31 (not_31_out, OPC1);
  not not_32 (not_32_out, SC2);
  not not_33 (not_33_out, SC2);
  not not_34 (not_34_out, SC2);
  not not_35 (not_35_out, SC1);
  not not_36 (not_36_out, SC0);
  not not_37 (not_37_out, OPC1);
  not not_38 (not_38_out, SC2);
  not not_39 (not_39_out, SC2);
  not not_40 (not_40_out, SC2);
  not not_41 (not_41_out, SC1);
  not not_42 (not_42_out, OPC1);
  not not_43 (not_43_out, SC1);
  not not_44 (not_44_out, SC0);
  not not_45 (not_45_out, SC1);
  not not_46 (not_46_out, SC0);
  not not_47 (not_47_out, OPC0);
  not not_48 (not_48_out, SC2);
  and and_1 (C0, not_1_out, not_2_out, not_3_out);
  and and_2 (and_2_out, not_4_out, SC0, not_5_out);
  and and_3 (and_3_out, OPC0, not_6_out, not_7_out, SC0);
  and and_4 (and_4_out, OPC1, not_8_out, not_9_out, SC0);
  and and_5 (C2, OPC1, OPC0, SC2, not_10_out, not_11_out);
  and and_6 (and_6_out, not_12_out, not_13_out, SC0);
  and and_7 (and_7_out, not_14_out, SC2, not_15_out, not_16_out);
  and and_8 (and_8_out, not_17_out, not_18_out, SC0);
  and and_9 (and_9_out, not_19_out, SC2, not_20_out, not_21_out);
  and and_10 (and_10_out, OPC1, OPC0, not_22_out, SC0);
  and and_11 (and_11_out, not_23_out, SC1, not_24_out);
  and and_12 (and_12_out, not_25_out, SC2, not_26_out, SC0);
  and and_13 (C6, OPC1, OPC0, SC2, not_27_out, not_28_out);
  and and_14 (C7, not_29_out, SC1, not_30_out);
  and and_15 (and_15_out, not_31_out, not_32_out, SC1, SC0);
  and and_16 (and_16_out, OPC0, not_33_out, SC1, SC0);
  and and_17 (and_17_out, not_34_out, not_35_out, not_36_out);
  and and_18 (and_18_out, not_37_out, not_38_out, SC1, SC0);
  and and_19 (and_19_out, OPC0, not_39_out, SC1, SC0);
  and and_20 (and_20_out, not_40_out, not_41_out, SC0);
  and and_21 (and_21_out, not_42_out, SC2, not_43_out, not_44_out);
  and and_22 (and_22_out, OPC0, SC2, not_45_out, not_46_out);
  and and_23 (C11, OPC1, not_47_out, not_48_out, SC1, SC0);
  or or_1 (C1, and_2_out, and_3_out, and_4_out);
  or or_2 (C3, and_6_out, and_7_out);
  or or_3 (C4, and_8_out, and_9_out, and_10_out);
  or or_4 (C5, and_11_out, and_12_out);
  or or_5 (C8, and_15_out, and_16_out);
  or or_6 (C9, and_17_out, and_18_out, and_19_out);
  or or_7 (C10, and_20_out, and_21_out, and_22_out);

  // Notes on the sheet:
  //   CU 1
endmodule

module CU_II (
  input  OPC3,
  input  OPC2,
  input  OPC1,
  input  OPC0,
  input  SC2,
  input  SC1,
  input  SC0,
  output C12,
  output C13,
  output C14,
  output C15
);

  wire not_1_out, not_2_out, not_3_out, not_4_out, not_5_out, not_6_out, not_7_out, not_8_out;

  not not_1 (not_1_out, OPC1);
  not not_2 (not_2_out, OPC0);
  not not_3 (not_3_out, SC1);
  not not_4 (not_4_out, OPC1);
  not not_5 (not_5_out, SC1);
  not not_6 (not_6_out, SC2);
  not not_7 (not_7_out, OPC0);
  not not_8 (not_8_out, SC2);
  and and_1 (C12, not_1_out, not_2_out, SC2, not_3_out, SC0);
  and and_2 (C13, not_4_out, OPC0, SC2, not_5_out, SC0);
  and and_3 (C14, OPC1, OPC0, not_6_out, SC1, SC0);
  and and_4 (C15, OPC1, not_7_out, not_8_out, SC1, SC0);

  // Notes on the sheet:
  //   CU 2
endmodule

module NEW_CPU_With_Improvements (
  input  [7:0] Data_1,
  input  [7:0] Data_2,
  input  in_3,
  input  in_4,
  input  in_5,
  input  in_6,
  input  in_7,
  input  in_8,
  input  in_9,
  input  Output_Enable,
  input  in_11,
  output Carry_out_plus,
  output Carry_out_minus,
  output [7:0] Carry_out_x,
  output [7:0] Data_Output,
  output [7:0] Carry_out,
  output [7:0] ALU_Result,
  output [2:0] function_Selector_Maulaually,
  output Zero_Flag
);

  wire C;
  wire [2:0] counter_3_q;
  wire [6:0] bit_extender_1_out;
  wire [7:0] adder_1_out, AND_out, counter_1_q, counter_2_q, counter_4_q, counter_5_q, divider_1_out,
       multiplier_1_out, OR_out, ram_1_data, subtractor_1_out, XOR_out;

  Clock clock_1 (.out(C));
  Counter #(.max('h8)) counter_1 (.count(in_3), .Q(counter_1_q), .clk(C));  // open: load, D, carry, clr
  Counter #(.max('h8)) counter_2 (.count(in_4), .Q(counter_2_q), .clk(C));  // open: load, D, carry, clr
  Adder adder_1 (.a(counter_1_q), .b(counter_2_q), .out(adder_1_out), .cout(Carry_out_plus));  // open: cin
  Subtractor subtractor_1 (
    .a(counter_1_q), .b(counter_2_q), .out(subtractor_1_out), .bout(Carry_out_minus));  // open: bin
  Multiplier multiplier_1 (.a(counter_1_q), .b(counter_2_q), .out(multiplier_1_out), .cout(Carry_out_x));  // open: cin
  Divider divider_1 (.a(counter_1_q), .b(counter_2_q), .out(divider_1_out), .rem(Carry_out));  // open: upper
  assign AND_out = counter_1_q & counter_2_q;  // AND_Gate AND, 8 bits wide
  assign OR_out = counter_1_q | counter_2_q;  // OR_Gate OR, 8 bits wide
  assign XOR_out = counter_1_q ^ counter_2_q;  // XOR_Gate XOR, 8 bits wide
  Multiplexer #(.select(3), .width(8)) multiplexer_1 (
    .in0(adder_1_out), .in1(subtractor_1_out), .in2(multiplier_1_out), .in3(divider_1_out), .in4(AND_out),
    .in5(OR_out), .in6(XOR_out), .out(ALU_Result), .sel(counter_3_q));  // open: in7, en
  Counter #(.width(3), .max('h7)) counter_3 (.count(in_11), .Q(counter_3_q), .clk(C));  // open: load, D, carry, clr
  assign Data_Output = Output_Enable ? ALU_Result : 8'bz;  // Controlled_Buffer controlled_buffer_1
  nor nor_1 (Zero_Flag, ALU_Result[0], ALU_Result[1], ALU_Result[2], ALU_Result[3], ALU_Result[4], ALU_Result[5], ALU_Result[6], ALU_Result[7]);
  LED led_1 (.in(ALU_Result[0]));
  LED led_2 (.in(ALU_Result[1]));
  LED led_3 (.in(ALU_Result[2]));
  LED led_4 (.in(ALU_Result[3]));
  LED led_5 (.in(ALU_Result[4]));
  LED led_6 (.in(ALU_Result[5]));
  LED led_7 (.in(ALU_Result[6]));
  LED led_8 (.in(ALU_Result[7]));
  Counter counter_4 (.count(in_6), .Q(counter_4_q), .clk(C));  // open: load, D, carry, clr
  Counter counter_5 (.D(ALU_Result), .count(in_7), .Q(counter_5_q), .clk(C));  // open: load, carry, clr
  Random random_1 (.clk(C), .next(in_5));  // open: out, clr
  RAM #(.bus("separate")) ram_1 (
    .addr(counter_4_q), .din(counter_5_q), .data(ram_1_data), .str(in_8), .clk(C), .ld(in_9));  // open: sel, clr
  Counter counter_6 (.D(ram_1_data), .clk(C));  // open: load, count, Q, carry, clr
  Bit_Extender #(.out_width(7)) bit_extender_1 (.in(ram_1_data), .out(bit_extender_1_out));
  TTY tty_1 (.data(bit_extender_1_out), .clk(C));  // open: we, clr

  // Notes on the sheet:
  //   Control Unit
  //   REDISTER
endmodule

module CU_for_JMP_And_JNZ (
  input  OPC3,
  input  OPC2,
  input  OPC1,
  input  OPC0,
  input  SC2,
  input  OPC3_2,
  input  OPC2_2,
  input  OPC1_2,
  input  OPC0_2,
  input  ZERO_FLAG,
  input  SC2_2,
  output C_JMP,
  output C_JNZ
);

  wire and_2_out, not_1_out, not_2_out, not_3_out, not_4_out, not_5_out, not_6_out;

  not not_1 (not_1_out, OPC3);
  not not_2 (not_2_out, OPC1);
  not not_3 (not_3_out, OPC0);
  not not_4 (not_4_out, OPC3_2);
  not not_5 (not_5_out, OPC1_2);
  and and_1 (C_JMP, not_1_out, OPC2, not_2_out, not_3_out, SC2);
  and and_2 (and_2_out, not_4_out, OPC2_2, not_5_out, OPC0_2, SC2_2);
  and and_3 (C_JNZ, and_2_out, not_6_out);
  not not_6 (not_6_out, ZERO_FLAG);

  // Notes on the sheet:
  //   JMP AND JNZ
endmodule
